# Fritzing sketch IMU (saved by Fritzing 0.9.3b)
breadboards: 1

parts:
  Mod1 = Raspberry Pi Pico
  M1 = gy9250

nets:
  N1: Mod1.pin_3, Mod1.pin_8, Mod1.pin_13, Mod1.pin_18, Mod1.pin_23, Mod1.pin_28, Mod1.pin_33, Mod1.pin_38, Mod1.pin_42, M1.pin2
  N2: Mod1.pin_6, M1.pin4
  N3: Mod1.pin_7, M1.pin3
  N4: Mod1.pin_36, M1.pin1

notes:
  SCL GP5
  SDA GP4

custom parts:
  Raspberry Pi Pico: Raspberry Pi Pico. Based around the RP2040 microcontroller the Pico is a low cost microcontroller device bringing Raspberry Pi quality, cost, and easy of use to the microcontroller space. Jan 2021, Split part in to two versions: tht (this one) and SMD. This one will drill holes for a .1 in header in pcb to allow plugging in the module as well as providing pads to solder the module to the top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
  gy9250: MPU-9250 module (three-axis gyroscope + three-axis acceleration + three-axis magnetic field). The generic model from ebay et. al. rather than the Sparkfun version.
